// Logisim project a.circ as structural Verilog: 1 circuit, main circuit main
module main (
  input  CLR,
  input  Vcc
);

  wire clock_1_out, t_ff_1_q, t_ff_2_q, t_ff_3_q, t_ff_4_q;

  Clock clock_1 (.out(clock_1_out));
  T_Flip_Flop #(.trigger("falling")) t_ff_1 (
    .clk(clock_1_out), .T(Vcc), .Q(t_ff_1_q), .reset(CLR));  // open: Qn, preset
  T_Flip_Flop #(.trigger("falling")) t_ff_2 (.clk(t_ff_1_q), .T(Vcc), .Q(t_ff_2_q), .reset(CLR));  // open: Qn, preset
  T_Flip_Flop #(.trigger("falling")) t_ff_3 (.clk(t_ff_2_q), .T(Vcc), .Q(t_ff_3_q), .reset(CLR));  // open: Qn, preset
  T_Flip_Flop #(.trigger("falling")) t_ff_4 (.clk(t_ff_3_q), .T(Vcc), .Q(t_ff_4_q), .reset(CLR));  // open: Qn, preset
  // Digital_Oscilloscope #(.nState(16)) digital_oscilloscope_1: pin names not known; wires that end beside it: t_ff_3_q, clock_1_out, t_ff_1_q, t_ff_2_q, t_ff_3_q, t_ff_4_q, Vcc, CLR
endmodule
