// Logisim project b.circ as structural Verilog: 1 circuit, main circuit main
module main (
);

  wire clock_1_out, t_ff_1_q, t_ff_2_q, t_ff_3_q, t_ff_4_q, Vcc_p1;

  Clock clock_1 (.out(clock_1_out));
  // DipSwitch #(.NSwitches(1)) Vcc: pin names not known; wires that end beside it: Vcc_p1
  T_Flip_Flop #(.trigger("falling")) t_ff_1 (
    .clk(clock_1_out), .T(Vcc_p1), .Q(t_ff_1_q), .reset(t_ff_4_q));  // open: Qn, preset
  T_Flip_Flop #(.trigger("falling")) t_ff_2 (
    .clk(t_ff_1_q), .T(Vcc_p1), .Q(t_ff_2_q), .reset(t_ff_4_q));  // open: Qn, preset
  T_Flip_Flop #(.trigger("falling")) t_ff_3 (
    .clk(t_ff_2_q), .T(Vcc_p1), .Q(t_ff_3_q), .reset(t_ff_4_q));  // open: Qn, preset
  T_Flip_Flop #(.trigger("falling")) t_ff_4 (
    .clk(t_ff_3_q), .T(Vcc_p1), .Q(t_ff_4_q), .reset(t_ff_4_q));  // open: Qn, preset
  // Digital_Oscilloscope #(.nState(16)) digital_oscilloscope_1: pin names not known; wires that end beside it: t_ff_3_q, clock_1_out, t_ff_1_q, t_ff_2_q, t_ff_3_q, t_ff_4_q, Vcc_p1
endmodule
