// Logisim project c.circ as structural Verilog: 1 circuit, main circuit main
module main (
);

  wire clock_1_out, Vcc_p1;
  wire [3:0] t_ff_1_q;

  Clock clock_1 (.out(clock_1_out));
  // DipSwitch #(.NSwitches(1)) Vcc: pin names not known; wires that end beside it: Vcc_p1
  T_Flip_Flop #(.trigger("falling")) t_ff_1 (
    .clk(clock_1_out), .T(Vcc_p1), .Q(t_ff_1_q[0]), .reset(t_ff_1_q[3]));  // open: Qn, preset
  T_Flip_Flop #(.trigger("falling")) t_ff_2 (
    .clk(t_ff_1_q[0]), .T(Vcc_p1), .Q(t_ff_1_q[1]), .reset(t_ff_1_q[3]));  // open: Qn, preset
  T_Flip_Flop #(.trigger("falling")) t_ff_3 (
    .clk(t_ff_1_q[1]), .T(Vcc_p1), .Q(t_ff_1_q[2]), .reset(t_ff_1_q[3]));  // open: Qn, preset
  T_Flip_Flop #(.trigger("falling")) t_ff_4 (
    .clk(t_ff_1_q[2]), .T(Vcc_p1), .Q(t_ff_1_q[3]), .reset(t_ff_1_q[3]));  // open: Qn, preset
  Hex_Digit_Display hex_digit_display_1 (.value(t_ff_1_q));  // open: dp
endmodule
