// Logisim project ContFF_T.circ as structural Verilog: 1 circuit, main circuit main
module main (
);

  wire CLK_out, CLR_p1, t_ff_1_q, t_ff_2_q, t_ff_3_q, t_ff_4_q;

  Clock CLK (.out(CLK_out));
  // DipSwitch #(.NSwitches(1)) CLR: pin names not known; wires that end beside it: CLR_p1
  LED Q0 (.in(t_ff_1_q));
  T_Flip_Flop #(.trigger("falling"), .NegatePresetClear("true")) t_ff_1 (
    .clk(CLK_out), .T(1'b1), .Q(t_ff_1_q), .reset(CLR_p1));  // open: Qn, preset
  LED Q1 (.in(t_ff_2_q));
  T_Flip_Flop #(.trigger("falling"), .NegatePresetClear("true")) t_ff_2 (
    .clk(t_ff_1_q), .T(1'b1), .Q(t_ff_2_q), .reset(CLR_p1));  // open: Qn, preset
  LED Q2 (.in(t_ff_3_q));
  T_Flip_Flop #(.trigger("falling"), .NegatePresetClear("true")) t_ff_3 (
    .clk(t_ff_2_q), .T(1'b1), .Q(t_ff_3_q), .reset(CLR_p1));  // open: Qn, preset
  LED Q3 (.in(t_ff_4_q));
  T_Flip_Flop #(.trigger("falling"), .NegatePresetClear("true")) t_ff_4 (
    .clk(t_ff_3_q), .T(1'b1), .Q(t_ff_4_q), .reset(CLR_p1));  // open: Qn, preset
endmodule
