// Logisim project ContFF_T_Módulo5.circ as structural Verilog: 1 circuit, main circuit main
module main (
);

  wire CLK_out, nand_1_out;
  wire [3:0] t_ff_1_q;

  Clock CLK (.out(CLK_out));
  T_Flip_Flop #(.trigger("falling"), .NegatePresetClear("true")) t_ff_1 (
    .clk(CLK_out), .T(1'b1), .Q(t_ff_1_q[0]), .reset(nand_1_out));  // open: Qn, preset
  Hex_Digit_Display hex_digit_display_1 (.value(t_ff_1_q));  // open: dp
  T_Flip_Flop #(.trigger("falling"), .NegatePresetClear("true")) t_ff_2 (
    .clk(t_ff_1_q[0]), .T(1'b1), .Q(t_ff_1_q[1]), .reset(nand_1_out));  // open: Qn, preset
  T_Flip_Flop #(.trigger("falling"), .NegatePresetClear("true")) t_ff_3 (
    .clk(t_ff_1_q[1]), .T(1'b1), .Q(t_ff_1_q[2]), .reset(nand_1_out));  // open: Qn, preset
  T_Flip_Flop #(.trigger("falling"), .NegatePresetClear("true")) t_ff_4 (
    .clk(t_ff_1_q[2]), .T(1'b1), .Q(t_ff_1_q[3]), .reset(nand_1_out));  // open: Qn, preset
  nand nand_1 (nand_1_out, t_ff_1_q[1], t_ff_1_q[2]);

  // Notes on the sheet:
  //   Q0
  //   Q1
  //   Q2
  //   Q3
endmodule
