// Logisim project ContFF_T_Módulo5_3FF_OSC.circ as structural Verilog: 1 circuit, main circuit main
module main (
);

  wire CLK_out, nand_1_out, t_ff_1_q, t_ff_2_q, t_ff_3_q;

  Clock CLK (.out(CLK_out));
  T_Flip_Flop #(.trigger("falling"), .NegatePresetClear("true")) t_ff_1 (
    .clk(CLK_out), .T(1'b1), .Q(t_ff_1_q), .reset(nand_1_out));  // open: Qn, preset
  T_Flip_Flop #(.trigger("falling"), .NegatePresetClear("true")) t_ff_2 (
    .clk(t_ff_1_q), .T(1'b1), .Q(t_ff_2_q), .reset(nand_1_out));  // open: Qn, preset
  T_Flip_Flop #(.trigger("falling"), .NegatePresetClear("true")) t_ff_3 (
    .clk(t_ff_2_q), .T(1'b1), .Q(t_ff_3_q), .reset(nand_1_out));  // open: Qn, preset
  nand nand_1 (nand_1_out, t_ff_3_q, t_ff_2_q);

  // Notes on the sheet:
  //   Q0
  //   Q1
  //   Q2
endmodule
