// Logisim project a.circ as structural Verilog: 1 circuit, main circuit main
module main (
);

  wire and_1_out, and_2_out, clock_1_out, digital_oscilloscope_1_p5, t_ff_1_q, t_ff_2_q, t_ff_3_q, Vcc_p1,
       Vcc_p2;

  Clock clock_1 (.out(clock_1_out));
  // DipSwitch #(.NSwitches(1)) Vcc: pin names not known; wires that end beside it: Vcc_p1, Vcc_p2
  T_Flip_Flop t_ff_1 (.clk(clock_1_out), .T(Vcc_p1), .Q(t_ff_1_q), .reset(Vcc_p2));  // open: Qn, preset
  T_Flip_Flop t_ff_2 (.clk(clock_1_out), .T(t_ff_1_q), .Q(t_ff_2_q));  // open: Qn, preset, reset
  and and_1 (and_1_out, t_ff_2_q, t_ff_1_q);
  T_Flip_Flop t_ff_3 (.clk(clock_1_out), .T(and_1_out), .Q(t_ff_3_q));  // open: Qn, preset, reset
  and and_2 (and_2_out, t_ff_3_q, t_ff_1_q, t_ff_2_q);
  // Digital_Oscilloscope #(.nState(16)) digital_oscilloscope_1: pin names not known; wires that end beside it: clock_1_out, t_ff_1_q, t_ff_2_q, t_ff_3_q, digital_oscilloscope_1_p5, Vcc_p1
  T_Flip_Flop t_ff_4 (.clk(clock_1_out), .T(and_2_out), .Q(digital_oscilloscope_1_p5));  // open: Qn, preset, reset
endmodule
