// Logisim project b.circ as structural Verilog: 1 circuit, main circuit main
module main (
);

  wire and_1_out, and_2_out, clock_1_out, Vcc_p1, Vcc_p2;
  wire [3:0] t_ff_1_q;

  Clock clock_1 (.out(clock_1_out));
  // DipSwitch #(.NSwitches(1)) Vcc: pin names not known; wires that end beside it: Vcc_p1, Vcc_p2
  T_Flip_Flop t_ff_1 (.clk(clock_1_out), .T(Vcc_p1), .Q(t_ff_1_q[0]), .reset(Vcc_p2));  // open: Qn, preset
  T_Flip_Flop t_ff_2 (.clk(clock_1_out), .T(t_ff_1_q[0]), .Q(t_ff_1_q[1]));  // open: Qn, preset, reset
  and and_1 (and_1_out, t_ff_1_q[1], t_ff_1_q[0]);
  T_Flip_Flop t_ff_3 (.clk(clock_1_out), .T(and_1_out), .Q(t_ff_1_q[2]));  // open: Qn, preset, reset
  and and_2 (and_2_out, t_ff_1_q[2], t_ff_1_q[0], t_ff_1_q[1]);
  T_Flip_Flop t_ff_4 (.clk(clock_1_out), .T(and_2_out), .Q(t_ff_1_q[3]));  // open: Qn, preset, reset
  Hex_Digit_Display hex_digit_display_1 (.value(t_ff_1_q));  // open: dp
endmodule
