// Logisim project Exercicio.circ as structural Verilog: 1 circuit, main circuit main
module main (
);

  wire and_1_out, CLK_out, clock_1_out, CLR_out, d_ff_4_q, d_ff_5_q, digital_oscilloscope_2_p1,
       digital_oscilloscope_2_p5, nand_1_out, not_1_out, not_2_out, not_3_out, Vcc_p1;
  wire [2:0] d_ff_1_q, t_ff_1_q;

  Button CLR (.out(CLR_out));
  nand nand_1 (nand_1_out, not_1_out, not_2_out, d_ff_1_q[2], d_ff_1_q[1], not_3_out);
  and and_1 (and_1_out, nand_1_out, CLK_out);
  Clock CLK (.out(CLK_out));
  // DipSwitch #(.NSwitches(1)) Vcc: pin names not known; wires that end beside it: Vcc_p1
  LED Q0 (.in(t_ff_1_q[0]));
  T_Flip_Flop #(.trigger("falling")) t_ff_1 (
    .clk(and_1_out), .T(Vcc_p1), .Q(t_ff_1_q[0]), .reset(CLR_out));  // open: Qn, preset
  not not_1 (not_1_out, d_ff_5_q);
  not not_2 (not_2_out, d_ff_4_q);
  not not_3 (not_3_out, d_ff_1_q[0]);
  LED Din (.in(t_ff_1_q[1]));
  LED Q1 (.in(t_ff_1_q[1]));
  T_Flip_Flop #(.trigger("falling")) t_ff_2 (
    .clk(t_ff_1_q[0]), .T(Vcc_p1), .Q(t_ff_1_q[1]), .reset(CLR_out));  // open: Qn, preset
  Hex_Digit_Display hex_digit_display_1 (.value({1'b0, d_ff_1_q}));  // open: dp
  LED Q2 (.in(t_ff_1_q[2]));
  T_Flip_Flop #(.trigger("falling")) t_ff_3 (
    .clk(t_ff_1_q[1]), .T(Vcc_p1), .Q(t_ff_1_q[2]), .reset(CLR_out));  // open: Qn, preset
  LED Q0_2 (.in(d_ff_1_q[0]));
  D_Flip_Flop #(.trigger("falling")) d_ff_1 (
    .clk(and_1_out), .D(t_ff_1_q[1]), .Q(d_ff_1_q[0]), .reset(CLR_out));  // open: Qn, preset
  Hex_Digit_Display hex_digit_display_2 (.value({1'b0, t_ff_1_q}));  // open: dp
  LED Q1_2 (.in(d_ff_1_q[1]));
  D_Flip_Flop #(.trigger("falling")) d_ff_2 (
    .clk(and_1_out), .D(d_ff_1_q[0]), .Q(d_ff_1_q[1]), .reset(CLR_out));  // open: Qn, preset
  LED Q2_2 (.in(d_ff_1_q[2]));
  D_Flip_Flop #(.trigger("falling")) d_ff_3 (
    .clk(and_1_out), .D(d_ff_1_q[1]), .Q(d_ff_1_q[2]), .reset(CLR_out));  // open: Qn, preset
  LED Q3 (.in(d_ff_4_q));
  D_Flip_Flop #(.trigger("falling")) d_ff_4 (
    .clk(and_1_out), .D(d_ff_1_q[2]), .Q(d_ff_4_q), .reset(CLR_out));  // open: Qn, preset
  LED Q4 (.in(d_ff_5_q));
  D_Flip_Flop #(.trigger("falling")) d_ff_5 (
    .clk(and_1_out), .D(d_ff_4_q), .Q(d_ff_5_q), .reset(CLR_out));  // open: Qn, preset
  Clock clock_1 (.out(clock_1_out));
  // Digital_Oscilloscope digital_oscilloscope_1: pin names not known; wires that end beside it: clock_1_out, d_ff_1_q[0], d_ff_1_q[1], d_ff_1_q[2], d_ff_4_q, d_ff_5_q
  // Digital_Oscilloscope digital_oscilloscope_2: pin names not known; wires that end beside it: digital_oscilloscope_2_p1, t_ff_1_q[2], t_ff_1_q[1], t_ff_1_q[0], digital_oscilloscope_2_p5, digital_oscilloscope_2_p5, CLR_out, CLR_out
  Clock clock_2 (.out(digital_oscilloscope_2_p1));
  // DipSwitch #(.NSwitches(1)) dipswitch_1: pin names not known; wires that end beside it: digital_oscilloscope_2_p5
endmodule
