// Logisim project FF_D_OSC_CLK.circ as structural Verilog: 1 circuit, main circuit main
module main (
);

  wire digital_oscilloscope_1_p1, digital_oscilloscope_1_p2, digital_oscilloscope_1_p3,
       digital_oscilloscope_1_p4;

  // Digital_Oscilloscope #(.nState(16)) digital_oscilloscope_1: pin names not known; wires that end beside it: digital_oscilloscope_1_p1, digital_oscilloscope_1_p2, digital_oscilloscope_1_p3, digital_oscilloscope_1_p4
  Clock CLK (.out(digital_oscilloscope_1_p1));
  Clock #(.highDuration(4), .lowDuration(4)) D (.out(digital_oscilloscope_1_p2));
  D_Flip_Flop d_ff_1 (
    .clk(digital_oscilloscope_1_p1), .D(digital_oscilloscope_1_p2), .Q(digital_oscilloscope_1_p3));  // open: Qn, preset, reset
  Button button_1 (.out(digital_oscilloscope_1_p4));
  LED Q (.in(digital_oscilloscope_1_p3));

  // Notes on the sheet:
  //   CLK
  //   D
  //   Q
endmodule
