// Logisim project Reg_FF_D_CargaParalela_LOAD.circ as structural Verilog: 1 circuit, main circuit main
module main (
  input  in_1,
  input  in_2,
  input  in_3
);

  wire CLK_p1, d_ff_1_q, d_ff_2_q, d_ff_3_q, LOAD_p1, multiplexer_1_out, multiplexer_2_out, multiplexer_3_out;

  // DipSwitch #(.NSwitches(1)) CLK: pin names not known; wires that end beside it: CLK_p1
  Multiplexer #(.enable("false")) multiplexer_1 (.in0(d_ff_1_q), .in1(in_1), .out(multiplexer_1_out), .sel(LOAD_p1));
  // DipSwitch #(.NSwitches(1)) LOAD: pin names not known; wires that end beside it: LOAD_p1
  LED Q0 (.in(d_ff_1_q));
  D_Flip_Flop #(.trigger("falling")) d_ff_1 (
    .clk(CLK_p1), .D(multiplexer_1_out), .Q(d_ff_1_q));  // open: Qn, preset, reset
  Multiplexer #(.enable("false")) multiplexer_2 (.in0(d_ff_2_q), .in1(in_2), .out(multiplexer_2_out), .sel(LOAD_p1));
  LED Q1 (.in(d_ff_2_q));
  D_Flip_Flop #(.trigger("falling")) d_ff_2 (
    .clk(CLK_p1), .D(multiplexer_2_out), .Q(d_ff_2_q));  // open: Qn, preset, reset
  Multiplexer #(.enable("false")) multiplexer_3 (.in0(d_ff_3_q), .in1(in_3), .out(multiplexer_3_out), .sel(LOAD_p1));
  LED Q2 (.in(d_ff_3_q));
  D_Flip_Flop #(.trigger("falling")) d_ff_3 (
    .clk(CLK_p1), .D(multiplexer_3_out), .Q(d_ff_3_q));  // open: Qn, preset, reset
endmodule
