// Logisim project Reg_FF_D_ParaleloSerie.circ as structural Verilog: 1 circuit, main circuit main
module main (
  input  in_1,
  input  in_2,
  input  in_3
);

  wire CLK_out, CLR_p1, d_ff_1_q, d_ff_2_q, d_ff_3_q, Enable_p1, nand_1_out, nand_2_out, nand_3_out;

  Clock CLK (.out(CLK_out));
  // DipSwitch #(.NSwitches(1)) Enable: pin names not known; wires that end beside it: Enable_p1
  // DipSwitch #(.NSwitches(1)) CLR: pin names not known; wires that end beside it: CLR_p1
  nand nand_1 (nand_1_out, Enable_p1, in_1);
  D_Flip_Flop #(.trigger("falling"), .NegatePresetClear("true")) d_ff_1 (
    .clk(CLK_out), .Q(d_ff_1_q), .preset(nand_1_out), .reset(CLR_p1));  // open: D, Qn
  nand nand_2 (nand_2_out, Enable_p1, in_2);
  D_Flip_Flop #(.trigger("falling"), .NegatePresetClear("true")) d_ff_2 (
    .clk(CLK_out), .D(d_ff_1_q), .Q(d_ff_2_q), .preset(nand_2_out), .reset(CLR_p1));  // open: Qn
  nand nand_3 (nand_3_out, Enable_p1, in_3);
  LED \Saída_Serial  (.in(d_ff_3_q));
  D_Flip_Flop #(.trigger("falling"), .NegatePresetClear("true")) d_ff_3 (
    .clk(CLK_out), .D(d_ff_2_q), .Q(d_ff_3_q), .preset(nand_3_out), .reset(CLR_p1));  // open: Qn
endmodule
