// Logisim project Reg_FF_D_SerieParalelo.circ as structural Verilog: 1 circuit, main circuit main
module main (
);

  wire CLK_p1, digital_oscilloscope_1_p2, digital_oscilloscope_1_p3, digital_oscilloscope_1_p4,
       digital_oscilloscope_1_p5, Din_p1;

  // DipSwitch #(.NSwitches(1)) CLK: pin names not known; wires that end beside it: CLK_p1
  // DipSwitch #(.NSwitches(1)) Din: pin names not known; wires that end beside it: Din_p1
  // Digital_Oscilloscope #(.nState(8)) digital_oscilloscope_1: pin names not known; wires that end beside it: CLK_p1, digital_oscilloscope_1_p2, digital_oscilloscope_1_p3, digital_oscilloscope_1_p4, digital_oscilloscope_1_p5
  LED Q0 (.in(digital_oscilloscope_1_p2));
  D_Flip_Flop #(.trigger("falling")) d_ff_1 (
    .clk(CLK_p1), .D(Din_p1), .Q(digital_oscilloscope_1_p2));  // open: Qn, preset, reset
  LED D0 (.in(Din_p1));
  Button button_1 (.out(digital_oscilloscope_1_p5));
  LED Q1 (.in(digital_oscilloscope_1_p3));
  D_Flip_Flop #(.trigger("falling")) d_ff_2 (
    .clk(CLK_p1), .D(digital_oscilloscope_1_p2), .Q(digital_oscilloscope_1_p3));  // open: Qn, preset, reset
  LED D1 (.in(digital_oscilloscope_1_p2));
  LED Q2 (.in(digital_oscilloscope_1_p4));
  D_Flip_Flop #(.trigger("falling")) d_ff_3 (
    .clk(CLK_p1), .D(digital_oscilloscope_1_p3), .Q(digital_oscilloscope_1_p4));  // open: Qn, preset, reset
  LED D2 (.in(digital_oscilloscope_1_p3));

  // Notes on the sheet:
  //   CLK
  //   Q0
  //   Q1
  //   Q2
endmodule
